# Fritzing sketch lampicka_no_connector (saved by Fritzing 0.9.3b)
circuit board: 2.39664cm x 2.16964cm
breadboards: 1

parts:
  Espessif_Serial_Wifi_Modul_1 = ESP8266 ESP01 [part_number=ESP8266 package=THT]
  C1 = SMD Capacitor [package=1206]
  C2 = SMD Capacitor [package=1206]
  R1 = Resistor [tolerance=±5% resistance=3.3k package="1206 [SMD]"]
  IC2 = Voltage Regulator LM1117 [package=sot223]
  Power_plug2 = Power plug
  RED = female alternating pin header, 1 pin [form="♀ (female)"]
  BLUE = female alternating pin header, 1 pin [form="♀ (female)"]
  GREEN = female alternating pin header, 1 pin [form="♀ (female)"]
  12V = female alternating pin header, 1 pin [form="♀ (female)"]
  R3 = Resistor [tolerance=±5% resistance=3.3k package="1206 [SMD]"]
  R4 = Resistor [tolerance=±5% resistance=4.7k package="1206 [SMD]"]
  R5 = Resistor [tolerance=±5% resistance=4.7k package="1206 [SMD]"]
  R6 = Resistor [tolerance=±5% resistance=4.7k package="1206 [SMD]"]
  R7 = Resistor [tolerance=±5% resistance=3.3k package="1206 [SMD]"]
  Součástka1 = IR Receiver Breakout [package=PCB]
  GND = female alternating pin header, 1 pin [form="♀ (female)"]
  IR = female alternating pin header, 1 pin [form="♀ (female)"]
  3_3V = rounded female pin header, 1 pin [form="♀ (female rounded)"]
  R8 = Resistor [tolerance=±5% resistance=10k package="1206 [SMD]"]
  R9 = Resistor [tolerance=±5% resistance=10k package="1206 [SMD]"]
  R10 = Resistor [tolerance=±5% resistance=10k package="1206 [SMD]"]
  Q1 = NPN-Transistor [package="SOT-23 [SMD]"]
  Q2 = NPN-Transistor [package="SOT-23 [SMD]"]
  Q3 = NPN-Transistor [package="SOT-23 [SMD]"]

nets:
  GND: Espessif_Serial_Wifi_Modul_1.GND, C1.2, C2.2, IC2.ADJ, Power_plug2.GND, Součástka1.GND, GND.pin1, R8.Pin_0, R9.Pin_0, R10.Pin_1, Q1.2, Q2.2, Q3.2
  N1: Espessif_Serial_Wifi_Modul_1.RXD, R6.Pin_1, R7.Pin_0
  N2: Espessif_Serial_Wifi_Modul_1.TXD, R3.Pin_0, R5.Pin_1
  3.3V: Espessif_Serial_Wifi_Modul_1.VCC, Espessif_Serial_Wifi_Modul_1.GPIO16, Espessif_Serial_Wifi_Modul_1.CH_PD, C2.1, R1.Pin_1, IC2.OUT, R3.Pin_1, R7.Pin_1, Součástka1.VCC, 3_3V.pin1
  N3: Espessif_Serial_Wifi_Modul_1.GPIO00, R1.Pin_0, R4.Pin_1
  N4: Espessif_Serial_Wifi_Modul_1.GPIO02, Součástka1.OUT, IR.pin1
  12V: C1.1, IC2.IN, Power_plug2.VCC, 12V.pin1
  N5: RED.pin1, Q2.1
  N6: BLUE.pin1, Q3.1
  N7: GREEN.pin1, Q1.1
  N8: R4.Pin_0, R8.Pin_1, Q1.0
  N9: R5.Pin_0, R9.Pin_1, Q3.0
  N10: R6.Pin_0, R10.Pin_0, Q2.0

custom parts:
  ESP8266 ESP01: Generic WiFi Module based on the ESP8266 with onboard PCB antenna and UART communications
  SMD Capacitor: Capacitor Standard 0603 ceramic capacitor, and 0.1 leaded capacitor.
  Power plug: power plug
